// Logisim project 4bitCPU.circ as structural Verilog: 8 circuits, main circuit main
module main (
  input  PC_IN
);

  wire and_1_out, and_2_out, clk, d_ff_1_q, d_ff_2_q, multiplexer_1_out, multiplexer_2_out, not_1_out,
       undriven, undriven_2, xor_1_out;

  Controlled_Buffer controlled_buffer_1 (.in(xor_1_out), .en(and_1_out));  // open: out
  Controlled_Buffer controlled_buffer_2 (.in(not_1_out), .en(and_1_out));  // open: out
  Multiplexer multiplexer_1 (.in0(not_1_out), .out(multiplexer_1_out), .sel(and_2_out));  // open: in1
  Controlled_Buffer controlled_buffer_3 (.in(1'b0), .en(and_1_out));  // open: out
  Controlled_Buffer controlled_buffer_4 (.in(1'b0), .en(and_1_out));  // open: out
  not not_1 (not_1_out, d_ff_1_q);
  D_Flip_Flop d_ff_1 (.D(multiplexer_1_out), .clk(clk), .Q(d_ff_1_q));  // open: Qn, preset, reset
  and and_1 (and_1_out, undriven, clk);
  xor xor_1 (xor_1_out, d_ff_2_q, d_ff_1_q);
  D_Flip_Flop d_ff_2 (.D(multiplexer_2_out), .clk(clk), .Q(d_ff_2_q));  // open: Qn, preset, reset
  Multiplexer multiplexer_2 (.in0(xor_1_out), .in1(undriven_2), .out(multiplexer_2_out), .sel(and_2_out));
  and and_2 (and_2_out, clk, PC_IN);
endmodule

module Half_adder (
  input  x,
  input  y,
  output S,
  output C
);

  xor xor_1 (S, x, y);
  and and_1 (C, x, y);
endmodule

module Full_adder (
  input  x,
  input  z,
  input  y,
  output S,
  output C
);

  wire half_adder_1_c, half_adder_1_s, half_adder_2_c;

  Half_adder half_adder_1 (.x(x), .y(y), .S(half_adder_1_s), .C(half_adder_1_c));
  Half_adder half_adder_2 (.x(half_adder_1_s), .y(z), .S(S), .C(half_adder_2_c));
  or or_1 (C, half_adder_2_c, half_adder_1_c);
endmodule

module two_bit_adder (
  input  x1,
  input  x0,
  input  y1,
  input  y0,
  input  Cin,
  output C,
  output s1,
  output s0
);

  wire full_adder_1_c;

  Full_adder full_adder_1 (.x(x0), .z(y0), .y(Cin), .S(s0), .C(full_adder_1_c));
  Full_adder full_adder_2 (.x(x1), .z(y1), .y(full_adder_1_c), .S(s1), .C(C));
endmodule

module two_bit_multiplier (
  input  x1,
  input  x0,
  input  y1,
  input  y0,
  output z0,
  output z1,
  output z2,
  output z3
);

  wire and_2_out, and_3_out, and_4_out, half_adder_1_c;

  and and_1 (z0, y0, x0);
  and and_2 (and_2_out, x1, y0);
  and and_3 (and_3_out, y1, x0);
  and and_4 (and_4_out, x1, y1);
  Half_adder half_adder_1 (.x(and_2_out), .y(and_3_out), .S(z1), .C(half_adder_1_c));
  Half_adder half_adder_2 (.x(and_4_out), .y(half_adder_1_c), .S(z2), .C(z3));
endmodule

module four_bit_adder_sub (
  input  add_sub,
  input  x3,
  input  x2,
  input  x1,
  input  x0,
  input  y3,
  input  y2,
  input  y1,
  input  y0,
  output C,
  output s3,
  output s2,
  output s1,
  output s0
);

  wire two_bit_adder_1_c, xor_1_out, xor_2_out, xor_3_out, xor_4_out;

  xor xor_1 (xor_1_out, y1, add_sub);
  xor xor_2 (xor_2_out, add_sub, y0);
  two_bit_adder two_bit_adder_1 (
    .x1(x1), .x0(x0), .y1(xor_1_out), .y0(xor_2_out), .Cin(add_sub), .C(two_bit_adder_1_c), .s1(s1), .s0(s0));
  xor xor_3 (xor_3_out, add_sub, y3);
  xor xor_4 (xor_4_out, y2, add_sub);
  two_bit_adder two_bit_adder_2 (
    .x1(x3), .x0(x2), .y1(xor_3_out), .y0(xor_4_out), .Cin(two_bit_adder_1_c), .C(C), .s1(s3), .s0(s2));
endmodule

module own_ram (
  input  WE,
  input  x3,
  input  x2,
  input  x1,
  input  x0,
  input  add_1,
  input  add_0,
  output y3,
  output y2,
  output y1,
  output y0
);

  wire and_1_out, and_2_out, and_3_out, and_4_out, and_5_out, and_6_out, and_7_out, and_8_out, and_9_out,
       and_10_out, and_11_out, and_12_out, and_13_out, and_14_out, and_15_out, and_16_out, and_17_out,
       and_18_out, and_19_out, and_20_out, and_21_out, and_22_out, and_23_out, and_24_out, d_ff_1_q,
       d_ff_2_q, d_ff_3_q, d_ff_4_q, d_ff_5_q, d_ff_6_q, d_ff_7_q, d_ff_8_q, d_ff_9_q, d_ff_10_q, d_ff_11_q,
       d_ff_12_q, d_ff_13_q, d_ff_14_q, d_ff_15_q, d_ff_16_q, not_1_out, not_2_out, not_3_out, not_4_out,
       undriven, undriven_2, undriven_3, undriven_4, undriven_5, undriven_6, undriven_7, undriven_8,
       undriven_9, undriven_10, undriven_11, undriven_12;

  not not_1 (not_1_out, add_0);
  not not_2 (not_2_out, add_1);
  not not_3 (not_3_out, add_1);
  not not_4 (not_4_out, add_0);
  and and_1 (and_1_out, not_1_out, not_2_out);
  and and_2 (and_2_out, add_0, not_3_out);
  and and_3 (and_3_out, not_4_out, add_1);
  and and_4 (and_4_out, add_0, add_1);
  and and_5 (and_5_out, and_1_out, WE);
  and and_6 (and_6_out, and_2_out, WE);
  and and_7 (and_7_out, and_3_out, WE);
  and and_8 (and_8_out, and_4_out, WE);
  D_Flip_Flop d_ff_1 (.D(x0), .clk(and_5_out), .Q(d_ff_1_q), .reset(undriven));  // open: Qn, preset
  D_Flip_Flop d_ff_2 (.D(x1), .clk(and_5_out), .Q(d_ff_2_q), .preset(undriven), .reset(undriven_2));  // open: Qn
  D_Flip_Flop d_ff_3 (.D(x2), .clk(and_5_out), .Q(d_ff_3_q), .preset(undriven_2), .reset(undriven_3));  // open: Qn
  D_Flip_Flop d_ff_4 (.D(x3), .clk(and_5_out), .Q(d_ff_4_q), .preset(undriven_3));  // open: Qn, reset
  D_Flip_Flop d_ff_5 (.D(x0), .clk(and_6_out), .Q(d_ff_5_q), .reset(undriven_4));  // open: Qn, preset
  D_Flip_Flop d_ff_6 (.D(x1), .clk(and_6_out), .Q(d_ff_6_q), .preset(undriven_4), .reset(undriven_5));  // open: Qn
  D_Flip_Flop d_ff_7 (.D(x2), .clk(and_6_out), .Q(d_ff_7_q), .preset(undriven_5), .reset(undriven_6));  // open: Qn
  D_Flip_Flop d_ff_8 (.D(x3), .clk(and_6_out), .Q(d_ff_8_q), .preset(undriven_6));  // open: Qn, reset
  D_Flip_Flop d_ff_9 (.D(x0), .clk(and_7_out), .Q(d_ff_9_q), .reset(undriven_7));  // open: Qn, preset
  D_Flip_Flop d_ff_10 (.D(x1), .clk(and_7_out), .Q(d_ff_10_q), .preset(undriven_7), .reset(undriven_8));  // open: Qn
  D_Flip_Flop d_ff_11 (.D(x2), .clk(and_7_out), .Q(d_ff_11_q), .preset(undriven_8), .reset(undriven_9));  // open: Qn
  D_Flip_Flop d_ff_12 (.D(x3), .clk(and_7_out), .Q(d_ff_12_q), .preset(undriven_9));  // open: Qn, reset
  D_Flip_Flop d_ff_13 (.D(x0), .clk(and_8_out), .Q(d_ff_13_q), .reset(undriven_10));  // open: Qn, preset
  D_Flip_Flop d_ff_14 (.D(x1), .clk(and_8_out), .Q(d_ff_14_q), .preset(undriven_10), .reset(undriven_11));  // open: Qn
  D_Flip_Flop d_ff_15 (.D(x2), .clk(and_8_out), .Q(d_ff_15_q), .preset(undriven_11), .reset(undriven_12));  // open: Qn
  D_Flip_Flop d_ff_16 (.D(x3), .clk(and_8_out), .Q(d_ff_16_q), .preset(undriven_12));  // open: Qn, reset
  and and_9 (and_9_out, and_1_out, d_ff_1_q);
  and and_10 (and_10_out, and_1_out, d_ff_2_q);
  and and_11 (and_11_out, and_1_out, d_ff_3_q);
  and and_12 (and_12_out, and_1_out, d_ff_4_q);
  and and_13 (and_13_out, and_2_out, d_ff_5_q);
  and and_14 (and_14_out, and_2_out, d_ff_6_q);
  and and_15 (and_15_out, and_2_out, d_ff_7_q);
  and and_16 (and_16_out, and_2_out, d_ff_8_q);
  and and_17 (and_17_out, and_3_out, d_ff_9_q);
  and and_18 (and_18_out, and_3_out, d_ff_10_q);
  and and_19 (and_19_out, and_3_out, d_ff_11_q);
  and and_20 (and_20_out, and_3_out, d_ff_12_q);
  and and_21 (and_21_out, and_4_out, d_ff_13_q);
  and and_22 (and_22_out, and_4_out, d_ff_14_q);
  and and_23 (and_23_out, and_4_out, d_ff_15_q);
  and and_24 (and_24_out, and_4_out, d_ff_16_q);
  or or_1 (y0, and_9_out, and_13_out, and_17_out, and_21_out);
  or or_2 (y1, and_10_out, and_14_out, and_18_out, and_22_out);
  or or_3 (y2, and_11_out, and_15_out, and_19_out, and_23_out);
  or or_4 (y3, and_12_out, and_16_out, and_20_out, and_24_out);
endmodule

module cpu_datapath (
  input  in_1,
  input  in_2,
  input  in_3,
  input  in_4,
  output out_5
);

  wire a_out, ALU_OUT_out, b_out, c_out, clk, clock_1_out, counter_1_carry, d_ff_1_q, d_ff_2_q, d_ff_3_q,
       d_ff_4_q, d_ff_5_q, d_ff_6_q, d_ff_7_q, d_ff_8_q, d_ff_13_q, d_ff_14_q, d_out, decoder_1_out0,
       decoder_1_out1, decoder_1_out2, decoder_1_out3, decoder_1_out4, decoder_1_out5, decoder_1_out6,
       decoder_1_out7, decoder_1_out8, decoder_1_out9, DISPLAY_IN_out, e_out, f_out, four_bit_adder_sub_1_c,
       four_bit_adder_sub_1_s0, four_bit_adder_sub_1_s1, four_bit_adder_sub_1_s2, four_bit_adder_sub_1_s3,
       g_out, IR_IN_out, IR_OUT_out, MAR_IN_out, not_1_out, PC_OUT_out, RAM_OUT_out, REG_X_IN_out,
       REG_X_OUT_out, REG_Y_IN_out, undriven, undriven_2, undriven_3, undriven_4, undriven_5, undriven_6,
       undriven_7, undriven_8, undriven_9;
  wire [1:0] counter_1_q, MAR_0_q;
  wire [3:0] counter_2_q, d_ff_9_q, ram_1_dout;
  wire [12:0] rom_1_data;

  RAM #(.addrWidth(2), .dataWidth(4)) ram_1 (
    .addr(MAR_0_q), .oe(RAM_OUT_out), .clk(clk), .dout(ram_1_dout));  // open: we, din
  Clock clock_1 (.out(clock_1_out));
  and MAR_IN (MAR_IN_out, rom_1_data[11], clk);
  and and_1 (clk, clock_1_out, not_1_out);
  not not_1 (not_1_out, rom_1_data[1]);
  D_Flip_Flop MAR_1 (.D(ram_1_dout[1]), .clk(MAR_IN_out), .Q(MAR_0_q[1]));  // open: Qn, preset, reset
  D_Flip_Flop MAR_0 (.D(ram_1_dout[0]), .clk(MAR_IN_out), .Q(MAR_0_q[0]));  // open: Qn, preset, reset
  and RAM_OUT (RAM_OUT_out, rom_1_data[10], clk);
  // Switch switch_1: pin names not known; wires that end beside it: in_1, ram_1_dout[3]
  // Switch switch_2: pin names not known; wires that end beside it: in_2, ram_1_dout[2]
  // Switch switch_3: pin names not known; wires that end beside it: in_3, ram_1_dout[1]
  // Switch switch_4: pin names not known; wires that end beside it: in_4, ram_1_dout[0]
  and REG_X_IN (REG_X_IN_out, rom_1_data[6], clk);
  D_Flip_Flop d_ff_1 (.D(ram_1_dout[3]), .clk(REG_X_IN_out), .Q(d_ff_1_q), .reset(undriven_4));  // open: Qn, preset
  D_Flip_Flop d_ff_2 (
    .D(ram_1_dout[2]), .clk(REG_X_IN_out), .Q(d_ff_2_q), .preset(undriven_4), .reset(undriven_5));  // open: Qn
  D_Flip_Flop d_ff_3 (
    .D(ram_1_dout[1]), .clk(REG_X_IN_out), .Q(d_ff_3_q), .preset(undriven_5), .reset(undriven_6));  // open: Qn
  D_Flip_Flop d_ff_4 (.D(ram_1_dout[0]), .clk(REG_X_IN_out), .Q(d_ff_4_q), .preset(undriven_6));  // open: Qn, reset
  D_Flip_Flop d_ff_5 (.D(ram_1_dout[3]), .clk(REG_Y_IN_out), .Q(d_ff_5_q), .reset(undriven_7));  // open: Qn, preset
  D_Flip_Flop d_ff_6 (
    .D(ram_1_dout[2]), .clk(REG_Y_IN_out), .Q(d_ff_6_q), .preset(undriven_7), .reset(undriven_8));  // open: Qn
  D_Flip_Flop d_ff_7 (
    .D(ram_1_dout[1]), .clk(REG_Y_IN_out), .Q(d_ff_7_q), .preset(undriven_8), .reset(undriven_9));  // open: Qn
  D_Flip_Flop d_ff_8 (.D(ram_1_dout[0]), .clk(REG_Y_IN_out), .Q(d_ff_8_q), .preset(undriven_9));  // open: Qn, reset
  assign ram_1_dout[0] = ALU_OUT_out ? four_bit_adder_sub_1_s0 : 1'bz;  // Controlled_Buffer controlled_buffer_1
  assign ram_1_dout[1] = ALU_OUT_out ? four_bit_adder_sub_1_s1 : 1'bz;  // Controlled_Buffer controlled_buffer_2
  assign ram_1_dout[2] = ALU_OUT_out ? four_bit_adder_sub_1_s2 : 1'bz;  // Controlled_Buffer controlled_buffer_3
  assign ram_1_dout[3] = ALU_OUT_out ? four_bit_adder_sub_1_s3 : 1'bz;  // Controlled_Buffer controlled_buffer_4
  D_Flip_Flop d_ff_9 (.D(ram_1_dout[0]), .clk(DISPLAY_IN_out), .Q(d_ff_9_q[0]), .reset(undriven));  // open: Qn, preset
  D_Flip_Flop d_ff_10 (
    .D(ram_1_dout[1]), .clk(DISPLAY_IN_out), .Q(d_ff_9_q[1]), .preset(undriven), .reset(undriven_2));  // open: Qn
  D_Flip_Flop d_ff_11 (
    .D(ram_1_dout[2]), .clk(DISPLAY_IN_out), .Q(d_ff_9_q[2]), .preset(undriven_2), .reset(undriven_3));  // open: Qn
  D_Flip_Flop d_ff_12 (
    .D(ram_1_dout[3]), .clk(DISPLAY_IN_out), .Q(d_ff_9_q[3]), .preset(undriven_3));  // open: Qn, reset
  Counter #(.max('h3), .width(2)) counter_1 (
    .load(1'b0), .up(1'b1), .count(rom_1_data[7]), .clk(clk), .D(ram_1_dout[1:0]), .carry(counter_1_carry),
    .Q(counter_1_q));  // open: clr
  assign ram_1_dout[0] = PC_OUT_out ? counter_1_q[0] : 1'bz;  // Controlled_Buffer controlled_buffer_5
  assign ram_1_dout[1] = PC_OUT_out ? counter_1_q[1] : 1'bz;  // Controlled_Buffer controlled_buffer_6
  D_Flip_Flop d_ff_13 (.D(ram_1_dout[0]), .clk(IR_IN_out), .Q(d_ff_13_q));  // open: Qn, preset, reset
  D_Flip_Flop d_ff_14 (.D(ram_1_dout[1]), .clk(IR_IN_out), .Q(d_ff_14_q));  // open: Qn, preset, reset
  D_Flip_Flop d_ff_15 (.D(ram_1_dout[2]), .clk(IR_IN_out), .Q(counter_2_q[2]));  // open: Qn, preset, reset
  D_Flip_Flop d_ff_16 (.D(ram_1_dout[3]), .clk(IR_IN_out), .Q(counter_2_q[3]));  // open: Qn, preset, reset
  and IR_IN (IR_IN_out, rom_1_data[9], clk);
  and IR_OUT (IR_OUT_out, rom_1_data[8], clk);
  assign ram_1_dout[0] = IR_OUT_out ? d_ff_13_q : 1'bz;  // Controlled_Buffer controlled_buffer_7
  assign ram_1_dout[1] = IR_OUT_out ? d_ff_14_q : 1'bz;  // Controlled_Buffer controlled_buffer_8
  and PC_OUT (PC_OUT_out, rom_1_data[12], clk);
  Counter #(.max('h3), .width(2)) counter_2 (
    .load(1'b0), .up(1'b1), .count(1'b1), .clk(clk), .Q(counter_2_q[1:0]));  // open: clr, D, carry
  and REG_Y_IN (REG_Y_IN_out, rom_1_data[4], clk);
  assign ram_1_dout[0] = REG_X_OUT_out ? d_ff_4_q : 1'bz;  // Controlled_Buffer controlled_buffer_9
  assign ram_1_dout[1] = REG_X_OUT_out ? d_ff_3_q : 1'bz;  // Controlled_Buffer controlled_buffer_10
  assign ram_1_dout[2] = REG_X_OUT_out ? d_ff_2_q : 1'bz;  // Controlled_Buffer controlled_buffer_11
  assign ram_1_dout[3] = REG_X_OUT_out ? d_ff_1_q : 1'bz;  // Controlled_Buffer controlled_buffer_12
  and REG_X_OUT (REG_X_OUT_out, clk, rom_1_data[5]);
  four_bit_adder_sub four_bit_adder_sub_1 (
    .add_sub(rom_1_data[0]), .x3(d_ff_1_q), .x2(d_ff_2_q), .x1(d_ff_3_q), .x0(d_ff_4_q), .y3(d_ff_5_q),
    .y2(d_ff_6_q), .y1(d_ff_7_q), .y0(d_ff_8_q), .C(four_bit_adder_sub_1_c), .s3(four_bit_adder_sub_1_s3),
    .s2(four_bit_adder_sub_1_s2), .s1(four_bit_adder_sub_1_s1), .s0(four_bit_adder_sub_1_s0));
  Decoder #(.select(4)) decoder_1 (
    .out0(decoder_1_out0), .out1(decoder_1_out1), .out2(decoder_1_out2), .out3(decoder_1_out3),
    .out4(decoder_1_out4), .out5(decoder_1_out5), .out6(decoder_1_out6), .out7(decoder_1_out7),
    .out8(decoder_1_out8), .out9(decoder_1_out9), .sel(d_ff_9_q), .en(1'b1));  // open: out10, out11, out12, out13, out14, out15
  and ALU_OUT (ALU_OUT_out, rom_1_data[3], clk);
  ROM #(.addrWidth(4), .dataWidth(13)) rom_1 (.addr(counter_2_q), .data(rom_1_data));
  and DISPLAY_IN (DISPLAY_IN_out, rom_1_data[2], clk);
  or a (a_out, decoder_1_out0, decoder_1_out2, decoder_1_out3, decoder_1_out5, decoder_1_out6, decoder_1_out7, decoder_1_out8, decoder_1_out9);
  or b (b_out, decoder_1_out0, decoder_1_out1, decoder_1_out2, decoder_1_out3, decoder_1_out4, decoder_1_out7, decoder_1_out8, decoder_1_out9);
  or c (c_out, decoder_1_out0, decoder_1_out1, decoder_1_out3, decoder_1_out4, decoder_1_out5, decoder_1_out6, decoder_1_out7, decoder_1_out8, decoder_1_out9);
  or d (d_out, decoder_1_out0, decoder_1_out2, decoder_1_out3, decoder_1_out5, decoder_1_out6, decoder_1_out8, decoder_1_out9);
  or e (e_out, decoder_1_out0, decoder_1_out2, decoder_1_out6, decoder_1_out8);
  or f (f_out, decoder_1_out0, decoder_1_out4, decoder_1_out5, decoder_1_out6, decoder_1_out8, decoder_1_out9);
  or g (g_out, decoder_1_out2, decoder_1_out3, decoder_1_out4, decoder_1_out5, decoder_1_out6, decoder_1_out8, decoder_1_out9);
  _7_Segment_Display u_7_segment_display_1 (
    .g(g_out), .f(f_out), .a(a_out), .b(b_out), .e(e_out), .d(d_out), .c(c_out), .dp(1'b0));

  // Notes on the sheet:
  //   contents of rom_1 (hex, n*v repeats v):
  //   1800 680 140 0 1800 680 110 48 1800 680 24 0 1800 680 2
endmodule
